# Fritzing sketch huzzah ws2811 (saved by Fritzing 0.9.2b)

parts:
  proto1 = Adafruit_PermaProto_1_4_Board
  Power_plug1 = Power plug
  C1 = Electrolytic Capacitor [capacitance=1mF package="100 mil [THT, electrolytic]"]  # not connected
  NEOPIXEL1 = Neopixel Strip -- White (60/m)
  74AHCT1 = 74AHCT125 [chip_label="74AHCT125 " package="DIP (Dual Inline) [THT]"]  # not connected
  Part2 = Adafruit HUZZAH ESP8266 [part_number="Adafruit #2471"]

nets:
  N1: proto1.connectorC13, proto1.connectorX13
  N2: proto1.connectorG10, NEOPIXEL1.+5V
  N3: proto1.connectorH9, Part2.GPIO13
  N4: proto1.connectorJ7, proto1.connectorY12
  N5: proto1.connectorJ8, proto1.connectorZ10
  N6: proto1.connectorX14, proto1.connectorZ14
  N7: proto1.connectorY1, NEOPIXEL1.DI
  N8: proto1.connectorY11, Part2.VBAT
  N9: proto1.connectorY15, Power_plug1.VCC
  N10: proto1.connectorZ1, NEOPIXEL1.GND
  N11: proto1.connectorZ12, Part2.GND
  N12: proto1.connectorZ15, Power_plug1.GND

custom parts:
  Neopixel Strip -- White (60/m): Neopixel Strip, White, 60 pixels per meter.
  74AHCT125: Quad Level-Shifter (3V to 5V)
  Adafruit HUZZAH ESP8266: Add Internet to your next project with an adorable, bite-sized WiFi microcontroller, at a price you like! The ESP8266 processor from Espressif is an 80 MHz microcontroller with a full WiFi front-end (both as client and access point) and TCP/IP stack with DNS support as well. While this chip has been very popular, its also been very difficult to use. Most of the low cost modules are not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
